# Fritzing sketch Hardware Diagram (saved by Fritzing 0.9.10b)

parts:
  L298N1 = L298N DC motor driver
  A1 = Teensy 4.1
  DC_Mot_Enc2 = DC Motor with two-phase encoder [part_number=VT-E-G25A-06-177E]
  Part1 = InvenSense MPU6050
  L298N2 = L298N DC motor driver
  DC_Mot_Enc3 = DC Motor with two-phase encoder [part_number=VT-E-G25A-06-177E]
  DC_Mot_Enc4 = DC Motor with two-phase encoder [part_number=VT-E-G25A-06-177E]
  DC_Mot_Enc5 = DC Motor with two-phase encoder [part_number=VT-E-G25A-06-177E]
  J1 = Basic Servo
  J2 = Basic Servo
  Part3 = I2C level shifter bidirectional
  J3 = Power Jack [package=power_jack_pth_lock]
  J5 = Power Jack [package=power_jack_pth_lock]
  Part4 = I2C level shifter bidirectional
  Part5 = I2C level shifter bidirectional
  RGB_SMD_LED1 = SMD RGB LED (WS2812) [package=5050]
  RGB_SMD_LED2 = SMD RGB LED (WS2812) [package=5050]
  RGB_SMD_LED3 = SMD RGB LED (WS2812) [package=5050]
  D1 = LTE-302 [package=lte-302]  # not connected
  D2 = LTE-302 [package=lte-302]  # not connected
  D3 = LTE-302 [package=lte-302]  # not connected
  D4 = LTE-302 [package=lte-302]  # not connected

nets:
  N1: L298N1.OUT1, DC_Mot_Enc5.Motor_Power_Terminal_+
  N2: L298N1.OUT2, DC_Mot_Enc5.Motor_Power_Terminal_-
  N3: L298N1.OUT3, DC_Mot_Enc2.Motor_Power_Terminal_-
  N4: L298N1.OUT4, DC_Mot_Enc2.Motor_Power_Terminal_+
  12V: L298N1.12V, L298N2.12V, J3.PWR
  GND: L298N1.GND, A1.Pin_10, A1.Pin_12, A1.Pin_38, A1.Pin_50, A1.Pin_63, DC_Mot_Enc2.Quad_Encoder_Ground, Part1.GND, L298N2.GND, DC_Mot_Enc3.Quad_Encoder_Ground, DC_Mot_Enc4.Quad_Encoder_Ground, DC_Mot_Enc5.Quad_Encoder_Ground, J1.gnd, J2.gnd, Part3.GND, J3.GND, J5.GND, Part4.GND, Part5.GND, RGB_SMD_LED1.VSS, RGB_SMD_LED2.VSS, RGB_SMD_LED3.VSS
  VCC: L298N1.5V, A1.Pin_64, DC_Mot_Enc2.Quad_Encoder_+5V, L298N2.5V, DC_Mot_Enc3.Quad_Encoder_+5V, DC_Mot_Enc4.Quad_Encoder_+5V, DC_Mot_Enc5.Quad_Encoder_+5V, J1.vcc, J2.vcc, Part3.HV, J5.PWR, Part4.HV, Part5.HV, RGB_SMD_LED1.VCC, RGB_SMD_LED1.VDD, RGB_SMD_LED2.VCC, RGB_SMD_LED2.VDD, RGB_SMD_LED3.VCC, RGB_SMD_LED3.VDD
  N5: L298N1.ENA, A1.Pin_18
  N6: L298N1.ENB, A1.Pin_61
  N7: L298N1.IN1, A1.Pin_58
  N8: L298N1.IN2, A1.Pin_59
  N9: L298N1.IN3, A1.Pin_29
  N10: L298N1.IN4, A1.Pin_30
  N11: A1.Pin_15, Part4.LV1
  N12: A1.Pin_16, Part4.LV2
  N13: A1.Pin_17, Part4.LV3
  N14: A1.Pin_19, Part4.LV4
  N15: A1.Pin_20, Part5.LV1
  N16: A1.Pin_21, Part5.LV2
  N17: A1.Pin_22, L298N2.ENB
  N18: A1.Pin_26, A1.Pin_37, A1.Pin_62, Part1.VCC, Part3.LV, Part4.LV, Part5.LV
  N19: A1.Pin_31, L298N2.ENA
  N20: A1.Pin_33, Part5.LV3
  N21: A1.Pin_34, Part5.LV4
  N22: A1.Pin_35, L298N2.IN2
  N23: A1.Pin_42, L298N2.IN3
  N24: A1.Pin_43, RGB_SMD_LED1.DIn
  N25: A1.Pin_44, Part3.LV1
  N26: A1.Pin_45, Part3.LV2
  N27: A1.Pin_48, L298N2.IN4
  N28: A1.Pin_49, L298N2.IN1
  N29: A1.Pin_56, Part1.SDA
  N30: A1.Pin_57, Part1.SCL
  N31: DC_Mot_Enc2.Quad_Encoder_A_Signal, Part4.HV3
  N32: DC_Mot_Enc2.Quad_Encoder_B_Signal, Part4.HV4
  N33: L298N2.OUT1, DC_Mot_Enc3.Motor_Power_Terminal_+
  N34: L298N2.OUT2, DC_Mot_Enc3.Motor_Power_Terminal_-
  N35: L298N2.OUT3, DC_Mot_Enc4.Motor_Power_Terminal_-
  N36: L298N2.OUT4, DC_Mot_Enc4.Motor_Power_Terminal_+
  N37: DC_Mot_Enc3.Quad_Encoder_A_Signal, Part5.HV1
  N38: DC_Mot_Enc3.Quad_Encoder_B_Signal, Part5.HV2
  N39: DC_Mot_Enc4.Quad_Encoder_A_Signal, Part5.HV3
  N40: DC_Mot_Enc4.Quad_Encoder_B_Signal, Part5.HV4
  N41: DC_Mot_Enc5.Quad_Encoder_A_Signal, Part4.HV1
  N42: DC_Mot_Enc5.Quad_Encoder_B_Signal, Part4.HV2
  N43: J1.pulse, Part3.HV2
  N44: J2.pulse, Part3.HV1
  N45: RGB_SMD_LED1.DOut, RGB_SMD_LED2.DIn
  N46: RGB_SMD_LED2.DOut, RGB_SMD_LED3.DIn

notes:
  STERO CAMERA PINS
  SDA
  SCL<module fritzingVersion="0.9.10b.2022-07-01.CD-2134-0-40d23c29">
  <boundingRects>
  <boundingRect rect="400.483 -250.526 26.717 57.0435" name="Breadboard View"/>
  <boundingRect rect="0 0 0 0" name="PCB View"/>
  <boundingRect rect="0 0 0 0" name="Schematic View"/>
  </boundingRects>
  <instances>
  <instance path=":/resources/parts/core/wire.fzp" moduleIdRef="WireModuleID" modelIndex="85524199">
  <title>Wire19</title>
  <views>
  <breadboardView layer="breadboardWire">
  <geometry x2="-17.6829" x1="0" y2="48.0095" z="3.50004" y1="0" y="-246.009" wireFlags="64" x="422.683"/>
  <wireExtras banded="0" opacity="1" mils="22.2222" color="#404040"/>
  <connectors>
  <connector layer="breadboardWire" connectorId="connector1">
  <geometry y="0" x="0"/>
  <connects/>
  </connector>
  </connectors>
  </breadboardView>
  <schematicView layer="schematicTrace">
  <geometry x2="-20.6675" x1="0" y2="43.335" z="5.50006" y1="0" y="-242.009" wireFlags="64" x="427.016"/>
  <wireExtras banded="0" opacity="1" mils="9.7222" color="#404040"/>
  <connectors>
  <connector layer="schematicTrace" connectorId="connector1">
  <geometry y="0" x="0"/>
  <connects/>
  </connector>
  </connectors>
  </schematicView>
  <pcbView layer="copper1trace">
  <geometry x2="-20.6675" x1="0" y2="43.335" z="9.50006" y1="0" y="-242.009" wireFlags="64" x="427.016"/>
  <wireExtras banded="0" opacity="1" mils="11.1111" color="#f2c600"/>
  <connectors>
  <connector layer="copper1trace" connectorId="connector1">
  <geometry y="0" x="0"/>
  <connects/>
  </connector>
  </connectors>
  </pcbView>
  </views>
  </instance>
  </instances>
  </module>
  INT
  FSYNC
  JETSON XAVIER NX EVEN PINS
  5.0 VDC (Pin 2)
  5.0 VDC
  GND
  UART1_TX
  UART1_RX
  I2S0_SCLK
  GND
  SPI1_CS1
  SPI1_CS0
  GND
  SPI1_MISO
  SPI0_CS0
  SPI0_CS1
  I2C0_SCL
  GND
  GPIO07
  GND
  UART1_CTS
  I2S0_SDIN
  I2S0_SDOUT (Pin 40)
  JETSON XAVIER NX ODD PINS
  3.3 VDC (Pin 1)
  I2C1_SDA
  I2C1_SCL
  GPIO9
  GND
  UART1_RTS
  SPI1_SCK
  GPIO12
  3.3 VDC
  SPI0_MOSI
  SPI0_MISO
  SPI0_SCK
  GND
  I2C0_SDA
  GPIO01
  GPIO11
  GPIO13
  I2S0_FS
  SPI1_MOSI
  GND (Pin 39)
  Wire colors are different here (coming off of the motor)
  Blue should be Yellow (as is on our robot)
  Green should be White
  Yellow should be Orange
  White should be Green
  VOLTAGE LEVELS REGULATED FROM BATTERY SUPPLY
  LEFT, 12-14V Power
  RIGHT, 5V Power
  Daisy Chain of RGB LED Driver Chips Continues..
  FRONT RIGHT
  FRONT LEFT
  BACK RIGHT
  BACK LEFT
  TILT SERVO
  PAN SERVO
  NOTE: LED DATAIN CANNOT BE DIRECTLY CONNECTED TO TEENSY. MUST USE 5V BUFFER TO BUMP 3V3 SIG TO 5V. MOSFET LOGIC LEVEL SHIFTERS WILL NOT WORK DUE TO SPEEDS.

custom parts:
  L298N DC motor driver: 2x DC motor driver with 78M05 positive voltage regulator (7..35 V) L298N: max 46 V, 2 A Set 5 V Enable jumper to enable 5 V regultor (needed for the L298N) and +5 V output at screw terminal or supply external +5 V at screw terminal Set ENA and/or ENB to +5 V to enable motor permanently or supply ENA and/or ENB with PWM signal IN1 and IN2 set rotation directory for motor A (OUT1/OUT2) IN2 and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
  Teensy 4.1: The Teensy is a complete USB-based microcontoller development system, in a very small footprint, capable of implementing many types of projects. All programming is done via the USB port. No special programmer is needed, only a standard micro-USB cable and a PC or Macintosh with a USB port.
